# Fritzing sketch main (saved by Fritzing 0.9.4)
breadboards: 2

parts:
  Part2 = Arduino Pro Mini (3.3V)
  CB1 = Electrolytic Capacitor [capacitance=2.2µF voltage=5V package="100 mil [THT, electrolytic]"]  # not connected
  CB0 = Electrolytic Capacitor [capacitance=2.2µF voltage=5V package="100 mil [THT, electrolytic]"]  # not connected
  CS = Electrolytic Capacitor [capacitance=200nF voltage=25V package="100 mil [THT, electrolytic]"]  # not connected
  AMS1117 = V_REG_LD1117VXX [package=78xxl]
  CL = Electrolytic Capacitor [capacitance=330nF voltage=25V package="100 mil [THT, electrolytic]"]
  RL = Resistor [tolerance=±5% resistance=6.8M package=THT]
  C1 = Ceramic Capacitor [capacitance=100nF package="100 mil [THT, multilayer]"]
  C12 = Electrolytic Capacitor [capacitance=10µF voltage=25V package="100 mil [THT, electrolytic]"]

nets:
  N1: Part2.GND, AMS1117.OUT, CL.-, RL.Pin_0, C1.0, C12.-
  N2: Part2.VCC, AMS1117.IN, C1.1, C12.+
  N3: CL.+, RL.Pin_1

notes:
  VLCD-OUT
  VLCD-IN
  VS+
  VS-
  VB01-
  VB1-
  VB1+
  VB0+
  VDD2/3
  VSS (GND)
  BM1
  BM0
  VDD
  WR[R/W]
  D4
  RST
  A0 / CD
  RD[E] / WR1
  CS0
  D7
  D5
  D6
  WR[R/W] / WR0
  D0
  D1
  D2
  D3
